# Fritzing sketch Untitled Sketch (saved by Fritzing 0.9.3b)
breadboards: 1

parts:
  Part1 = Arduino Uno (Rev3) - ICSP
  Part2 = Bluetooth HC-05 Macho
  J2 = Basic Servo
  VCC1 = Battery block 9V
  VCC2 = 4 x AAA Battery Mount
  VCC3 = 4 x AAA Battery Mount
  J3 = Basic Servo
  J1 = Basic Servo

nets:
  GND: Part1.GND, Part2.GND, J2.gnd, VCC1.-, VCC2.-, VCC3.-, J3.gnd, J1.gnd
  N1: Part1.D0/RX, Part2.TXD
  N2: Part1.D1/TX, Part2.RXD
  N3: Part1.D3_PWM, J3.pulse
  N4: Part1.D4, J1.pulse
  N5: Part1.D5_PWM, J2.pulse
  N6: Part1.VIN, VCC1.+
  N7: Part2.VCC, VCC2.+
  VCC: J2.vcc, VCC3.+, J3.vcc, J1.vcc
